// Digital circuit ALU.dig as structural Verilog
// The Arithmetic Logic Unit (ALU) component, which can perform various operations on the provided operands, also determining the resulting flag values.
module ALU (
  input  [31:0] B,
  input  [31:0] A,
  input  [2:0] Opcode,
  output [31:0] Result,
  output Carry,
  output Negative,
  output Zero,
  output Overflow
);

  wire add_1_c_o, add_2_c_o, and_2_out, and_3_out, and_4_out, and_5_out, and_6_out, and_7_out, and_8_out,
       and_9_out, or_2_out, or_3_out, rotateleft_1_c, shiftleft_1_c, shiftright_1_c, xor_2_out, xor_3_out;
  wire [31:0] add_1_s, add_2_s, and_1_out, not_1_out, or_1_out, rotateleft_1_out, shiftleft_1_out,
       shiftright_1_out, xor_1_out;

  assign not_1_out = ~B;  // Not not_1, 32 bits wide
  assign or_1_out = A | B;  // Or or_1, 32 bits wide
  assign xor_1_out = A ^ B;  // XOr xor_1, 32 bits wide
  assign and_1_out = A & B;  // And and_1, 32 bits wide
  ShiftLeft shiftleft_1 (.A(A), .B(B), .Out(shiftleft_1_out), .C(shiftleft_1_c));
  ShiftRight shiftright_1 (.A(A), .B(B), .Out(shiftright_1_out), .C(shiftright_1_c));
  RotateLeft rotateleft_1 (.A(A), .B(B), .Out(rotateleft_1_out), .C(rotateleft_1_c));
  Add #(.Bits(32)) add_1 (.a(A), .b(B), .c_i(1'b0), .s(add_1_s), .c_o(add_1_c_o));
  Add #(.Bits(32)) add_2 (.a(A), .b(not_1_out), .c_i(1'b1), .s(add_2_s), .c_o(add_2_c_o));
  and and_2 (and_2_out, A[31], B[31]);
  and and_3 (and_3_out, ~A[31], ~B[31]);  // And
  and and_4 (and_4_out, B[31], Negative);
  and and_5 (and_5_out, ~B[31], ~Negative);  // And
  xor xor_2 (xor_2_out, Carry, Negative);
  xor xor_3 (xor_3_out, Carry, Negative);
  and and_6 (and_6_out, and_2_out, ~Negative);  // And
  and and_7 (and_7_out, Negative, and_3_out);
  and and_8 (and_8_out, and_4_out, ~A[31]);  // And
  and and_9 (and_9_out, A[31], and_5_out);
  or or_2 (or_2_out, and_6_out, and_7_out);
  or or_3 (or_3_out, and_8_out, and_9_out);
  Multiplexer #(.Selector_Bits(3), .Bits(32)) multiplexer_1 (
    .sel(Opcode), .in_0(or_1_out), .in_1(xor_1_out), .in_2(and_1_out), .in_3(shiftleft_1_out),
    .in_4(shiftright_1_out), .in_5(rotateleft_1_out), .in_6(add_1_s), .in_7(add_2_s),
    .out({Negative, Result[30:0]}));
  Multiplexer #(.Selector_Bits(3)) multiplexer_2 (
    .sel(Opcode), .in_0(1'b0), .in_1(1'b0), .in_2(1'b0), .in_3(shiftleft_1_c), .in_4(shiftright_1_c),
    .in_5(rotateleft_1_c), .in_6(add_1_c_o), .in_7(add_2_c_o), .out(Carry));
  Comparator #(.Bits(32)) comparator_1 (.a({32{1'b0}}), .b({Negative, Result[30:0]}), .eq(Zero));  // open: gt, lt
  Multiplexer #(.Selector_Bits(3)) multiplexer_3 (
    .sel(Opcode), .in_0(1'b0), .in_1(1'b0), .in_2(1'b0), .in_3(xor_2_out), .in_4(B[31]), .in_5(xor_3_out),
    .in_6(or_2_out), .in_7(or_3_out), .out(Overflow));

  assign Result[31] = Negative;

  // Notes on the sheet:
  //   B: The value of the ALU B operand.
  //   A: The value of the ALU A operand.
  //   Result: The resuling value, containing the value computed by the ALU.
  //   Carry: The resulting carry flag.
  //   Negative: The resulting negative flag.
  //   Zero: The resulting zero flag.
  //   Opcode: The ALU opcode, which specifies the operation to perform.
  //   Overflow: The resulting overflow flag.
endmodule

/* Test case Sub:
A B Opcode Result Carry Overflow Negative Zero

loop(i, 256)
    # determine random values for A and B inputs
    let a = random(1<<32);
    let b = random(1<<32);

    # compute expected Result
    let r = a + (~b & 0xffffffff) + 1;

    # determine expected flags
    let c = (r) >= (1<<32);
    let o = (((a>>31)&1) != ((b>>31)&1)) & (((a>>31)&1) != ((r>>31)&1));
    let n = (r>>31) & 1;
    let z = r=0;

    # perform subtraction, and then check Result and flags are as expected
    (a) (b) 7 (r) (c) (o) (n) (z)
end loop
*/

/* Test case Rol:
A B Opcode Result Carry Overflow Negative Zero

loop(i, 256)
    # determine random values for A and B inputs
    let a = random(1<<32);
    let b = random(1<<32);

    # compute expected Result
    let rot = a&31;
    let r = (b << rot) | (b >> (32-rot));

    # determine expected flags
    let c = ite(a = 0, 0, r & 1);
    let o = c != ((r>>31)&1);
    let n = (r>>31) & 1;
    let z = r=0;

    # perform rotation, and then check Result and flags are as expected
    (a) (b) 5 (r) (c) (o) (n) (z)
end loop

loop(i, 16)
    # determine random values for inputs
    # set A to 0 to test edge case for Carry flag
    let a = 0;
    let b = random(1<<32);

    # compute expected Result
    let rot = a&31;
    let r = (b << rot) | (b >> (32-rot));

    # determine expected flags
    let c = ite(a = 0, 0, r & 1);
    let o = c != ((r>>31)&1);
    let n = (r>>31) & 1;
    let z = r=0;

    # perform rotation, and then check Result and flags are as expected
    (a) (b) 5 (r) (c) (o) (n) (z)
end loop
*/

/* Test case Shr:
A B Opcode Result Carry Overflow Negative Zero

loop(i, 256)
    # determine random values for A and B inputs
    let a = random(1<<32) & 0x3f;
    let b = random(1<<32);

    # compute expected Result
    let r = ite((a >= 0 & a <= 32), ((b >> a) & 0xffffffff), 0);

    # determine expected flags
    let c = ite(a = 0 | a > 32, 0, (b >> (a-1)) & 1);
    let o = (b>>31) & 1;
    let n = (r>>31) & 1;
    let z = r=0;

    # perform logical shift right, and then check Result and flags are as expected
    (a) (b) 4 (r) (c) (o) (n) (z)
end loop
*/

/* Test case Shl:
A B Opcode Result Carry Overflow Negative Zero

loop(i, 256)
    # determine random values for A and B inputs
    let a = random(1<<32) & 0x3f;
    let b = random(1<<32);

    # compute expected Result
    let r = ite((a >= 0 & a <= 32), (b << a) & 0xffffffff, 0);

    # determine expected flags
    let c = ite(a = 0 | a > 32, 0, (b >> (32-a)) & 1);
    let o = c != ((r>>31)&1);
    let n = (r>>31) & 1;
    let z = r=0;

    # perform logical shift left, and then check Result and flags are as expected
    (a) (b) 3 (r) (c) (o) (n) (z)
end loop
*/
