// Digital circuit AReg.dig as structural Verilog
module AReg (
  input  [2:0] Type,
  input  [31:0] In,
  input  F,
  output [3:0] RA
);

  wire [3:0] multiplexer_1_out;

  Multiplexer #(.Selector_Bits(3), .Bits(4)) multiplexer_1 (
    .sel(Type), .in_0(4'b0000), .in_1(4'b0000), .in_2(In[15:12]), .in_3(4'b0000), .in_4(4'b0000),
    .in_5(In[15:12]), .in_6(4'b0000), .in_7(4'b0000), .out(multiplexer_1_out));
  Multiplexer #(.Bits(4)) multiplexer_2 (.sel(F), .in_0(multiplexer_1_out), .in_1(4'b0000), .out(RA));
  // Pins of 1 and 4 bits meet at RA
endmodule
