// Digital circuit CPU.dig as structural Verilog
module CPU (
  input  Clock,
  input  [31:0] Databus_in,
  output [31:0] Databus_out,
  output RE,
  output WE,
  output Halted,
  output [31:0] Addressbus
);

  wire ALU_carry, ALU_negative, ALU_overflow, ALU_zero, and_1_out, and_2_out, FlagRegisterBank_carry_out,
       FlagRegisterBank_negative_out, FlagRegisterBank_overflow_out, FlagRegisterBank_zero_out,
       InstructionDecoder_arith, InstructionDecoder_flags, InstructionDecoder_halted, or_1_out,
       Tester_testsucceeds, Timer_execute, Timer_fetch;
  wire [2:0] InstructionDecoder_opcode;
  wire [3:0] InstructionDecoder_condition, InstructionDecoder_reg_a, InstructionDecoder_reg_b,
       InstructionDecoder_reg_dest;
  wire [31:0] ALU_result, InstructionDecoder_constant, multiplexer_1_out, multiplexer_2_out,
       RegisterBank_data_b;

  Timer Timer (
    .Clock(Clock), .TestSucceeds(Tester_testsucceeds), .Halt(InstructionDecoder_halted), .Halted(Halted),
    .Fetch(Timer_fetch), .Execute(Timer_execute));
  Multiplexer #(.Bits(32)) multiplexer_1 (
    .sel(and_1_out), .in_0(ALU_result), .in_1(Databus_in), .out(multiplexer_1_out));
  and and_1 (and_1_out, RE, ~Timer_fetch);  // And
  InstructionDecoder InstructionDecoder (
    .Instruction(Databus_in), .Fetch(Timer_fetch), .Execute(Timer_execute), .Clock(Clock),
    .Condition(InstructionDecoder_condition), .Reg_A(InstructionDecoder_reg_a),
    .Reg_B(InstructionDecoder_reg_b), .Reg_dest(InstructionDecoder_reg_dest),
    .Opcode(InstructionDecoder_opcode), .Flags(InstructionDecoder_flags),
    .Constant(InstructionDecoder_constant), .WE(WE), .RE(RE), .Arith(InstructionDecoder_arith),
    .HALTED(InstructionDecoder_halted));
  RegisterBank RegisterBank (
    .Data_in(multiplexer_1_out), .Reg_dest(InstructionDecoder_reg_dest), .Reg_B(InstructionDecoder_reg_b),
    .Reg_A(InstructionDecoder_reg_a), .Clock(Clock), .Data_B(RegisterBank_data_b), .Data_A(Databus_out));
  FlagRegisterBank FlagRegisterBank (
    .Carry_in(ALU_carry), .Overflow_in(ALU_overflow), .Negative_in(ALU_negative), .Zero_in(ALU_zero),
    .Set(InstructionDecoder_flags), .Clock(Clock), .Carry_out(FlagRegisterBank_carry_out),
    .Overflow_out(FlagRegisterBank_overflow_out), .Negative_out(FlagRegisterBank_negative_out),
    .Zero_out(FlagRegisterBank_zero_out));
  Multiplexer #(.Bits(32)) multiplexer_2 (
    .sel(InstructionDecoder_arith), .in_0(Databus_out), .in_1(InstructionDecoder_constant),
    .out(multiplexer_2_out));
  ALU ALU (
    .B(RegisterBank_data_b), .A(multiplexer_2_out), .Opcode(InstructionDecoder_opcode), .Result(ALU_result),
    .Carry(ALU_carry), .Negative(ALU_negative), .Zero(ALU_zero), .Overflow(ALU_overflow));
  Tester Tester (
    .Carry(FlagRegisterBank_carry_out), .Overflow(FlagRegisterBank_overflow_out),
    .Negative(FlagRegisterBank_negative_out), .Zero(FlagRegisterBank_zero_out),
    .Condition(InstructionDecoder_condition), .TestSucceeds(Tester_testsucceeds));
  Multiplexer #(.Bits(32)) multiplexer_3 (
    .sel(or_1_out), .in_0(RegisterBank_data_b), .in_1(ALU_result), .out(Addressbus));
  or or_1 (or_1_out, and_2_out, WE);
  and and_2 (and_2_out, RE, ~Timer_fetch);  // And

  // Notes on the sheet:
  //   Databus_out: The databus signal from the CPU. Any values written by the CPU will be stored here.
  //   Databus_in: The databus signal to the CPU. Any values read (or instructions fetched) by the CPU will be stored here.
  //   RE: Read enabled signal. When a read operation is performed by the CPU this value is set to high.
  //   WE: Write enabled signal. When a write operation is performed by the CPU this value is set to high.
  //   Halted: Determines whether the CPU is in the halted state, in which it shall remain until the CPU is restarted.
  //   Addressbus: The addressbus signal, which determines the address of a read or write operation. For a write operation the address is where a value being written by the CPU should be stored. For a read operation the address is where a value being read by the CPU should be read from.
endmodule

/* Test case init:
# Minimal test case to sanity check that the CPU starts fetching from address 0 after starting the simulation.
Clock Databus_in Halted RE WE Databus_out Addressbus
0     0          0      1  0  x           0
*/

/* Test case add:
# The first line of test data must be the header, which contains the inputs and outputs used in the test case.
# In this case 'Clock' and 'Databus_in' are inputs; the rest are outputs.
# It is possible to use registers in test cases by enabling their 'use as measurement value' attribute in the advanced tab.
# The R0-R15 registers have this attribute enabled in the provided template.
# By adding R3 as an output in the header below, we can test whether it holds a certain value.

Clock Databus_in Halted RE WE Databus_out Addressbus R3

# These init statements are used to set the register contents when the simulation is started.
# Note that all init statements are collected and executed first. Interleaving them with regular test data has no effect.
# If you wish to test other instructions, or with different values, you must add a new test case component to the circuit.
# If you do not do this, the tests will run sequentially, meaning the next test will use the CPU state obtained after executing the prior test.
# This is reflected below in the last test data row that checks if the program counter increased by 4.
init R1=4;
init R2=5;

# ADD R1, R2, R3
# The four test data lines below describe the testing of the ADD R1, R2, R3 instruction.
# We first load the machine code into the Databus_in, and then drive the clock to step through the full instruction cycle once.
# Note that the first two columns (in this case) are inputs, meaning they will be set to the provided value.
# The other columns are outputs, which are evaluated after the inputs have been set, and then compared against the given expected values.
# The value 'x' denotes a 'do not care' value. Please click the 'Help' button in this dialog for more information regarding test cases.
0     0x6400123f 0      1  0  x           0          x
1     0x6400123f 0      x  x  x           x          x
0     0          0      0  0  x           x          x
1     0          0      0  0  x           x          9

# Fetch next instruction, check if the program counter increased by 4...
0     0          0      1  0  x           4          x
*/

/* Test case program:
# This test case has been generated by a script.
# It simulates the execution of a .hex file, and checks if your CPU behaves as expected.
# It is a good test once you think your CPU is completed, but do note that passing this test case does not mean your CPU does not have any bugs!
# If anything does go wrong with your CPU, you will likely get significant compounding errors.
# You should focus your attention on the earliest test fail, investigate + fix that, and then re-run the test case.
# All fails after this earliest fail may not be actual issues with your CPU, but just compounding errors.
# Since this test case only tests the high level behavior of your CPU, you may have to do some investigation as to why a test fails.
# An issue with your ALU producing incorrect flags for example may impact whether an instruction is skipped or not.
# This would manifest itself as fetching the next instruction rather than executing the current one (or the other way around); not as an issue with the ALU.
# As such first determine _what_ is going wrong on a high level, then try to track down _why_ this is happening.

# generated from hex file strcat.hex
Databus_in Clock Addressbus Databus_out RE WE Halted R0         R1         R2         R3         R4         R5         R6         R7         R8         R9         R10        R11        R12        R13        R14        R15        PHASE

# 001 fetch
0x016800ef 0     0x00000000 X           1  0  0      0x00000000 0x00000000 0x00000000 0x00000000 0x00000000 0x00000000 0x00000000 0x00000000 0x00000000 0x00000000 0x00000000 0x00000000 0x00000000 0x00000000 0x00000000 0x00000000 0

# 001 test
# or.t 168, r0, r14 (test succeeds: 1)
0x016800ef 1     X          X           X  X  0      0x00000000 0x00000000 0x00000000 0x00000000 0x00000000 0x00000000 0x00000000 0x00000000 0x00000000 0x00000000 0x00000000 0x00000000 0x00000000 0x00000000 0x00000000 0x00000004 1

# 001 execute
0x016800ef 0     X          X           0  0  0      0x00000000 0x00000000 0x00000000 0x00000000 0x00000000 0x00000000 0x00000000 0x00000000 0x00000000 0x00000000 0x00000000 0x00000000 0x00000000 0x00000000 0x00000000 0x00000004 2

# 001 pause
0x016800ef 1     X          X           X  X  0      0x00000000 0x00000000 0x00000000 0x00000000 0x00000000 0x00000000 0x00000000 0x00000000 0x00000000 0x00000000 0x00000000 0x00000000 0x00000000 0x00000000 0x00000168 0x00000004 3

# 002 fetch
0x0110007f 0     0x00000004 X           1  0  0      0x00000000 0x00000000 0x00000000 0x00000000 0x00000000 0x00000000 0x00000000 0x00000000 0x00000000 0x00000000 0x00000000 0x00000000 0x00000000 0x00000000 0x00000168 0x00000004 0

# 002 test
# or.t 110, r0, r7 (test succeeds: 1)
0x0110007f 1     X          X           X  X  0      0x00000000 0x00000000 0x00000000 0x00000000 0x00000000 0x00000000 0x00000000 0x00000000 0x00000000 0x00000000 0x00000000 0x00000000 0x00000000 0x00000000 0x00000168 0x00000008 1

# 002 execute
0x0110007f 0     X          X           0  0  0      0x00000000 0x00000000 0x00000000 0x00000000 0x00000000 0x00000000 0x00000000 0x00000000 0x00000000 0x00000000 0x00000000 0x00000000 0x00000000 0x00000000 0x00000168 0x00000008 2

# 002 pause
0x0110007f 1     X          X           X  X  0      0x00000000 0x00000000 0x00000000 0x00000000 0x00000000 0x00000000 0x00000000 0x00000110 0x00000000 0x00000000 0x00000000 0x00000000 0x00000000 0x00000000 0x00000168 0x00000008 3

# 003 fetch
0x00f4006f 0     0x00000008 X           1  0  0      0x00000000 0x00000000 0x00000000 0x00000000 0x00000000 0x00000000 0x00000000 0x00000110 0x00000000 0x00000000 0x00000000 0x00000000 0x00000000 0x00000000 0x00000168 0x00000008 0

# 003 test
# or.t f4, r0, r6 (test succeeds: 1)
0x00f4006f 1     X          X           X  X  0      0x00000000 0x00000000 0x00000000 0x00000000 0x00000000 0x00000000 0x00000000 0x00000110 0x00000000 0x00000000 0x00000000 0x00000000 0x00000000 0x00000000 0x00000168 0x0000000c 1

# 003 execute
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*/

/* Test case fetch 4 instr:
# The machine code 0 (32 zero bits) decodes to 'OR.F 0, R0, R0'.
# This is effectively a 'NOP.F', which due to the '.F' condition is always skipped.
# The tests below simulates the Fetch and Test phases four times in a row for this machine code.
# We never move into the Execute phase as the condition test fails during the Test phase.
# Each subsequent Fetch should fetch the next instruction however, which is the goal of this test case.
# Since we have fixed size 32-bit (4 byte) instructions, the 'next' fetch should fetch from the memory address 4 bytes past the last fetch.
# As we start fetching from address 0 initially when the CPU is started, this means we attempt to fetch from addresses 4, 8, and 12 next.

Clock Databus_in Halted RE WE Databus_out Addressbus
0     0          0      1  0  0           0
1     0          0      x  x  x           x
0     0          0      1  0  0           4
1     0          0      x  x  x           x
0     0          0      1  0  0           8
1     0          0      x  x  x           x
0     0          0      1  0  0           12
1     0          0      x  x  x           x
*/
