// Digital circuit Constant.dig as structural Verilog
module Constant (
  input  [2:0] Type,
  input  [31:0] In,
  input  F,
  output [31:0] Const
);

  wire [31:0] bitextender_1_out, multiplexer_1_out;

  BitExtender #(.inputBits(10), .outputBits(32)) bitextender_1 (.in(In[25:16]), .out(bitextender_1_out));
  Multiplexer #(.Selector_Bits(3), .Bits(32)) multiplexer_1 (
    .sel(Type), .in_0({32{1'b0}}), .in_1({32{1'b0}}), .in_2(bitextender_1_out), .in_3(bitextender_1_out),
    .in_4({In[29:8], {10{1'b0}}}), .in_5({32{1'b0}}), .in_6(bitextender_1_out), .in_7({32{1'b0}}),
    .out(multiplexer_1_out));
  Multiplexer #(.Bits(32)) multiplexer_2 (.sel(F), .in_0(multiplexer_1_out), .in_1(32'h4), .out(Const));
endmodule
