// Digital circuit Flags.dig as structural Verilog
module Flags (
  input  [2:0] Type,
  input  [31:0] In,
  input  F,
  output Flag
);

  wire multiplexer_1_out;

  Multiplexer #(.Selector_Bits(3)) multiplexer_1 (
    .sel(Type), .in_0(1'b0), .in_1(1'b0), .in_2(1'b0), .in_3(1'b0), .in_4(1'b0), .in_5(In[27]),
    .in_6(In[27]), .in_7(1'b0), .out(multiplexer_1_out));
  Multiplexer multiplexer_2 (.sel(F), .in_0(multiplexer_1_out), .in_1(1'b0), .out(Flag));
endmodule
