// Digital circuit Format.dig as structural Verilog
module Format (
  input  [31:0] In,
  output [2:0] Format
);

  wire and_1_out, and_2_out, and_3_out, and_4_out, and_5_out, and_6_out, comparator_1_eq, comparator_2_eq,
       comparator_3_eq, comparator_4_eq, comparator_5_eq, comparator_6_eq, comparator_7_eq;

  Comparator #(.Bits(28)) comparator_1 (.a({28{1'b1}}), .b(In[31:4]), .eq(comparator_1_eq));  // open: gt, lt
  Comparator #(.Bits(4)) comparator_2 (.a(4'b1000), .b(In[29:26]), .eq(comparator_2_eq));  // open: gt, lt
  Comparator #(.Bits(4)) comparator_3 (.a(In[7:4]), .b(4'b0000), .eq(comparator_3_eq));  // open: gt, lt
  Comparator #(.Bits(4)) comparator_4 (.a(In[29:26]), .b(4'b0000), .eq(comparator_4_eq));  // open: gt, lt
  Comparator #(.Bits(4)) comparator_5 (.a(In[15:12]), .b(4'b0000), .eq(comparator_5_eq));  // open: gt, lt
  Comparator #(.Bits(10)) comparator_6 (.a(In[25:16]), .b({10{1'b0}}), .eq(comparator_6_eq));  // open: gt, lt
  and and_1 (and_1_out, In[30], In[31]);
  and and_2 (and_2_out, ~In[30], In[31]);  // And
  Comparator #(.Bits(32)) comparator_7 (.a(In), .b({32{1'b0}}), .eq(comparator_7_eq));  // open: gt, lt
  and and_3 (and_3_out, comparator_2_eq, and_1_out, comparator_3_eq);
  and and_4 (and_4_out, comparator_4_eq, and_1_out, comparator_5_eq);
  and and_5 (and_5_out, ~In[31], comparator_6_eq, In[26]);  // And
  and and_6 (and_6_out, ~In[31], comparator_5_eq, ~In[26]);  // And
  PriorityEncoder #(.Selector_Bits(3)) priorityencoder_1 (
    .in0(1'b1), .in1(comparator_1_eq), .in2(and_3_out), .in3(and_4_out), .in4(and_2_out), .in5(and_5_out),
    .in6(and_6_out), .in7(comparator_7_eq), .num(Format));  // open: any
endmodule
