// Digital circuit InstructionDecoder.dig as structural Verilog
// The InstructionDecoder component, which serves as a hub to control many of the signals to other components. It implements both the fetch operation, and execution of machine code (including decoding).
module InstructionDecoder (
  input  [31:0] Instruction,
  input  Fetch,
  input  Execute,
  input  Clock,
  output [3:0] Condition,
  output [3:0] Reg_A,
  output [3:0] Reg_B,
  output [3:0] Reg_dest,
  output [2:0] Opcode,
  output Flags,
  output [31:0] Constant,
  output WE,
  output RE,
  output Arith,
  output HALTED
);

  wire comparator_2_eq;
  wire [2:0] format_1_format;
  wire [31:0] IR_q, multiplexer_1_out;

  Register #(.Bits(32)) IR (.D(Instruction), .C(Clock), .en(Fetch), .Q(IR_q));
  Multiplexer #(.Bits(32)) multiplexer_1 (.sel(Execute), .in_0({32{1'b0}}), .in_1(IR_q), .out(multiplexer_1_out));
  Format format_1 (.In(multiplexer_1_out), .Format(format_1_format));
  // AReg areg_1: pin names not known; wires that end beside it: format_1_format, multiplexer_1_out, Fetch, Reg_A
  // BReg breg_1: pin names not known; wires that end beside it: format_1_format, multiplexer_1_out, Fetch, Reg_B
  // DReg dreg_1: pin names not known; wires that end beside it: format_1_format, multiplexer_1_out, Fetch, Reg_dest
  Opcode opcode_1 (.Type(format_1_format), .In(multiplexer_1_out), .F(Fetch), .Op(Opcode));
  Flags flags_1 (.Type(format_1_format), .In(multiplexer_1_out), .F(Fetch), .Flag(Flags));
  Constant constant_1 (.Type(format_1_format), .In(multiplexer_1_out), .F(Fetch), .Const(Constant));
  Comparator #(.Bits(3)) comparator_1 (.a(3'b010), .b(format_1_format), .eq(WE));  // open: gt, lt
  Comparator #(.Bits(3)) comparator_2 (.a(3'b011), .b(format_1_format), .eq(comparator_2_eq));  // open: gt, lt
  Comparator #(.Bits(3)) comparator_3 (.a(3'b001), .b(format_1_format), .eq(HALTED));  // open: gt, lt
  or or_1 (RE, Fetch, comparator_2_eq);
  nand nand_1 (Arith, multiplexer_1_out[26], ~multiplexer_1_out[31]);  // NAnd

  assign Condition = Instruction[3:0];

  // Notes on the sheet:
  //   Condition: Instruction condition output, which contains the condition under which the instruction should be executed.
  //   Instruction: The instruction machine code input. If the CPU is in the fetch phase and a rising clock signal occurs, this machine code is stored in the internal instruction register (IR), so that it can be decoded and executed.
  //   Reg_A: A register output, which determines the register to be used for the first operand.
  //   Reg_B: B register output, which determines the register to be used for the second operand.
  //   Reg_dest: Destination register output, which determines the register that should store the result of a data operation. A data operation is either an ALU computation, or a read from an external device, such as RAM.
  //   Opcode: Opcode output, which determines the operation the ALU should perform.
endmodule
