// Digital circuit Opcode.dig as structural Verilog
module Opcode (
  input  [2:0] Type,
  input  [31:0] In,
  input  F,
  output [2:0] Op
);

  wire [2:0] multiplexer_1_out;

  Multiplexer #(.Selector_Bits(3), .Bits(3)) multiplexer_1 (
    .sel(Type), .in_0(3'b000), .in_1(3'b000), .in_2(3'b110), .in_3(3'b110), .in_4(3'b110), .in_5(In[30:28]),
    .in_6(In[30:28]), .in_7(3'b000), .out(multiplexer_1_out));
  Multiplexer #(.Bits(3)) multiplexer_2 (.sel(F), .in_0(multiplexer_1_out), .in_1(3'b110), .out(Op));
endmodule
