// Digital circuit RotateLeft.dig as structural Verilog
// Performs a rotate left of B by A places
module RotateLeft (
  input  [31:0] A,
  input  [31:0] B,
  output [31:0] Out,
  output C
);

  wire bitselector_1_out, comparator_1_eq;

  BarrelShifter #(.Bits(32), .barrelShifterMode("rotate")) barrelshifter_1 (.in(B), .shift(A[5:0]), .out(Out));
  Comparator #(.Bits(32)) comparator_1 (.a(A), .b({32{1'b0}}), .eq(comparator_1_eq));  // open: gt, lt
  BitSelector #(.Selector_Bits(5)) bitselector_1 (.in(Out), .sel({5{1'b0}}), .out(bitselector_1_out));
  and and_1 (C, bitselector_1_out, ~comparator_1_eq);  // And

  // Notes on the sheet:
  //   A: The A operand
  //   B: The B operand
  //   Out: The output value
  //   C: The carry value
endmodule

/* Test case:
A B Out C

loop(i, 256)
    # determine random values for A and B inputs
    let a = random(1<<32);
    let b = random(1<<32);

    # compute expected Result
    let rot = a&31;
    let r = (b << rot) | (b >> (32-rot));

    # determine expected flag
    let c = ite(a = 0, 0, r & 1);

    # perform rotate left, and then check Result and carry flag are as expected
    (a) (b) (r) (c)
end loop
*/
