// Digital circuit ShiftRight.dig as structural Verilog
// Performs a logical shift right of B by A places, i.e. B >> A
module ShiftRight (
  input  [31:0] A,
  input  [31:0] B,
  output [31:0] Out,
  output C
);

  wire bitselector_1_out, comparator_1_eq, comparator_2_gt, or_1_out;
  wire [31:0] barrelshifter_1_out, sub_1_s;

  Comparator #(.Bits(32)) comparator_1 (.a(A), .b({32{1'b0}}), .eq(comparator_1_eq));  // open: gt, lt
  Comparator #(.Bits(32)) comparator_2 (.a(A), .b(32'h20), .gt(comparator_2_gt));  // open: eq, lt
  Sub #(.Bits(32)) sub_1 (.a(A), .b(32'h1), .c_i(1'b0), .s(sub_1_s));  // open: c_o
  BarrelShifter #(.Bits(32), .direction("right")) barrelshifter_1 (.in(B), .shift(A[5:0]), .out(barrelshifter_1_out));
  or or_1 (or_1_out, comparator_1_eq, comparator_2_gt);
  BitSelector #(.Selector_Bits(5)) bitselector_1 (.in(B), .sel(sub_1_s[4:0]), .out(bitselector_1_out));
  Multiplexer #(.Bits(32)) multiplexer_1 (
    .sel(comparator_2_gt), .in_0(barrelshifter_1_out), .in_1({32{1'b0}}), .out(Out));
  and and_1 (C, ~or_1_out, bitselector_1_out);  // And

  // Notes on the sheet:
  //   A: The A operand
  //   B: The B operand
  //   Out: The output value
  //   C: The carry value
endmodule

/* Test case:
A B Out C

loop(i, 256)
    # determine random values for A and B inputs
    let a = random(1<<32) & 0x1f;
    let b = random(1<<32);

    # compute expected Result
    let r = ite((a >= 0 & a <= 32), ((b >> a) & 0xffffffff), 0);

    # determine expected flag
    let c = ite(a = 0 | a > 32, 0, (b >> (a-1)) & 1);

    # perform logical shift right, and then check Result and carry flag are as expected
    (a) (b) (r) (c)
end loop

loop(i, 128)
    # determine random values for A and B inputs
    let a = 32;
    let b = random(1<<32);

    # compute expected Result
    let r = ite((a >= 0 & a <= 32), ((b >> a) & 0xffffffff), 0);

    # determine expected flag
    let c = ite(a = 0 | a > 32, 0, (b >> (a-1)) & 1);

    # perform logical shift right, and then check Result and carry flag are as expected
    (a) (b) (r) (c)
end loop

loop(i, 128)
    # determine random values for A and B inputs
    let a = random(1<<32);
    let b = random(1<<32);

    # compute expected Result
    let r = ite((a >= 0 & a <= 32), ((b >> a) & 0xffffffff), 0);

    # determine expected flag
    let c = ite(a = 0 | a > 32, 0, (b >> (a-1)) & 1);

    # perform logical shift right, and then check Result and carry flag are as expected
    (a) (b) (r) (c)
end loop
*/
