// Digital circuit TimerTransitions.dig as structural Verilog
// Circuit that implements the state transitions of the timer FSM.
// Unused states transition to the Halted state.
module TimerTransitions (
  input  [2:0] Phase,
  input  TestSucceeds,
  input  Halt,
  output [2:0] Phase_2
);

  wire and_1_out, and_2_out, and_3_out, and_4_out, decoder_1_out_0, decoder_1_out_1, decoder_1_out_2,
       decoder_1_out_3, decoder_1_out_4, decoder_1_out_5, decoder_1_out_6, decoder_1_out_7, or_1_out,
       or_2_out;

  Decoder #(.Selector_Bits(3)) decoder_1 (
    .sel(Phase), .out_0(decoder_1_out_0), .out_1(decoder_1_out_1), .out_2(decoder_1_out_2),
    .out_3(decoder_1_out_3), .out_4(decoder_1_out_4), .out_5(decoder_1_out_5), .out_6(decoder_1_out_6),
    .out_7(decoder_1_out_7));
  and and_1 (and_1_out, decoder_1_out_2, Halt);
  or or_1 (or_1_out, decoder_1_out_4, decoder_1_out_5, decoder_1_out_6, decoder_1_out_7, and_1_out);
  and and_2 (and_2_out, decoder_1_out_2, ~Halt);  // And
  and and_3 (and_3_out, decoder_1_out_1, TestSucceeds);
  and and_4 (and_4_out, decoder_1_out_1, ~TestSucceeds);  // And
  or or_2 (or_2_out, decoder_1_out_3, and_4_out);
  PriorityEncoder #(.Selector_Bits(3)) priorityencoder_1 (
    .in0(or_2_out), .in1(decoder_1_out_0), .in2(and_3_out), .in3(and_2_out), .in4(or_1_out), .in5(1'b0),
    .in6(1'b0), .in7(1'b0), .num(Phase_2));  // open: any

  // Notes on the sheet:
  //   Phase: The current state of the timer.
  //   TestSucceeds: The current TestSucceeds signal value.
  //   Halt: The current Halt signal value.
  //   Phase_2: The new state of the timer.
  //   Fetch
  //   Test
  //   Execute
  //   Pause
  //   Halted
endmodule

/* Test case:
TestSucceeds Halt Phase Phase'
0            0    0     1
0            0    1     0
0            0    2     3
0            0    3     0
0            0    4     4
0            0    5     4
0            0    6     4
0            0    7     4
0            1    0     1
0            1    1     0
0            1    2     4
0            1    3     0
0            1    4     4
0            1    5     4
0            1    6     4
0            1    7     4
1            0    0     1
1            0    1     2
1            0    2     3
1            0    3     0
1            0    4     4
1            0    5     4
1            0    6     4
1            0    7     4
1            1    0     1
1            1    1     2
1            1    2     4
1            1    3     0
1            1    4     4
1            1    5     4
1            1    6     4
1            1    7     4
*/
